# Fritzing sketch Wiring (saved by Fritzing 0.9.3b)
breadboards: 1

parts:
  U1 = ESP32S-HiLetgo [part_number=ESP32S-HiLetgo]
  A1 = DHT22 module
  F1 = Fan - Ventilador [package=THT]
  F2 = Fan - Ventilador [package=THT]
  A2 = Dryer heater
  Part1 = Solar Panel [package="Renogy 50 Watts 12 Volt Monocrystalline Bendable Solar Panel"]
  Mod1 = Solar Charge Controller [part_number="KLD Series Solar Charge Controller PWM" package=PWM-Model]
  M1 = 1 chan 5v relay module
  M2 = 1 chan 5v relay module
  BAT1 = 12 battery [package=battery]  # not connected
  S1 = Round Pushbutton
  S2 = Round Pushbutton
  S3 = Round Pushbutton
  M3 = RioRand LM2596
  LCD2004-I2C1 = LCD2004-I2C

nets:
  GND: U1.GND, A1.-, M1.pin_2, M2.pin_2, S1.leg0, S2.leg0, S3.leg0, M3.Pin_4, LCD2004-I2C1.GND
  N1: U1.GPIO4, S2.leg1
  N2: U1.GPIO16, S1.leg1
  N3: U1.GPIO17, S3.leg1
  N4: U1.GPIO18, M2.pin_3
  N5: U1.GPIO19, M1.pin_3
  N6: U1.GPIO21, LCD2004-I2C1.SDA
  N7: U1.GPIO22, LCD2004-I2C1.SCL
  N8: U1.GPIO23, A1.Out
  N9: A1.+, M1.pin_1, M2.pin_1, M3.Pin_3, LCD2004-I2C1.VCC
  5V: F1.5V, F2.5V, M2.pin_6
  GND_2: F1.GND, F2.GND, A2.Pin_1, Mod1.Connector_6, M3.Pin_2
  N10: A2.Pin_2, M1.pin_6
  N11: Part1.Connector_1, Mod1.Connector_1
  N12: Part1.Connector_2, Mod1.Connector_2
  N13: Mod1.Connector_5, M1.pin_5, M2.pin_5, M3.Pin_1

custom parts:
  ESP32S-HiLetgo: HiLetgo ESP-WROOM-32 ESP32 ESP-32S Development Board 2.4GHz Dual-Mode WiFi + Bluetooth Dual Cores Microcontroller The ESP32 integrated with Antenna switches, RF Balun, power amplifiers, low-noise amplifiers, filters, and management modules, and the entire solution occupies the least area of PCB. 2.4 GHz Wi-Fi plus Bluetooth dual-mode chip, with TSMC Ultra-low power consumption 40nm technology,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
  DHT22 module: DHT22 module. Pins VCC Data GND.
  Fan - Ventilador: Ventilador de 2 pines, se encuentra comunmente en computadoras de escritorio
  Dryer heater: Dryer heater.
  Solar Panel: Renogy 50 Watts 12 Volt Solar Panel
  Solar Charge Controller: PWM-Solar Charge Controller
  1 chan 5v relay module: 1 Channel 5V Relay Module Board Shield with Optocoupler Support High and Low Level Trigger for Arduino.
  12 battery: 12V lead acid type battery, like the Husqvarna YTH2448 12V 35AH battery. This is the mini version 1/4 the size of the actual battery to be closer to typical breadboard parts (around 2in wide rathher than 7in). The pads in pcb are sized to accomidate up to 14ga wire (as these batterys will deliver high currents.)
  LCD2004-I2C: A standard character display with 4x20 characters. Comes in many colors with LCM2004 IIC attached.
